// Logisim project projet.circ as structural Verilog: 12 circuits, main circuit main
module main (
  input  Reset,
  input  ResetRAM,
  input  [15:0] PC
);

  wire and_1_out, Call, Clock, Clock_out, Cond, CTRL, Exec, Fetch, getcst_1_imm, Load, or_1_out,
       ramctrl_1_memload, ramctrl_1_memstore, Ret, Store, WriteReg;
  wire [2:0] GetOp, MemReg;
  wire [15:0] adder_1_out, adder_2_out, Addr, alu_1_output, getcst_1_cst, JMP_Address, MemIN,
       multiplexer_1_out, multiplexer_2_out, PC_t, R0, R1, R2, R3, R4, R5, R6, R7, registres_1_out_sr1,
       registres_1_out_sr2, regval_1_arith, SP, SP_1, StackAddr, subtractor_1_out, subtractor_2_out;
  wire [31:0] bit_extender_1_out, IR, MemOUT;

  Clock u_Clock (.out(Clock_out));
  Seq seq_1 (.ClockOrig(Clock_out), .reset(Reset), .Fetch(Fetch), .Exec(Exec), .Clock(Clock));
  LED led_1 (.in(Clock_out));
  LED led_2 (.in(Fetch));
  LED led_3 (.in(Exec));
  or or_1 (or_1_out, Call, Ret);
  // Probe on regval_1_arith
  RegVal regval_1 (
    .R0(R0), .R1(R1), .R2(R2), .R3(R3), .R4(R4), .R5(R5), .Reg(MemReg), .R6(R6), .R7(R7),
    .Arith(regval_1_arith));
  // Probe on MemReg
  and and_1 (and_1_out, or_1_out, Fetch);
  // Probe on PC_t
  // Probe on IR
  Adder #(.width(16)) adder_1 (.a(SP), .b(16'h1), .out(adder_1_out));  // open: cin, cout
  assign SP_1 = Call ? adder_1_out : 16'bz;  // Controlled_Buffer controlled_buffer_1
  assign SP_1 = Ret ? subtractor_1_out : 16'bz;  // Controlled_Buffer controlled_buffer_2
  Subtractor #(.width(16)) subtractor_1 (.a(SP), .b(16'h1), .out(subtractor_1_out));  // open: bin, bout
  Register #(.width(16)) register_1 (.D(SP_1), .en(and_1_out), .Q(SP), .clk(Clock), .clr(Reset));
  RegPC regpc_1 (
    .JMP_Address(JMP_Address), .Cond(Cond), .CTRL(CTRL), .Clock(Exec), .Reset(Reset), .PC(PC_t), .Call(Call),
    .RET_Address(StackAddr), .RET(Ret));
  // Probe on PC_t
  GetAddr getaddr_1 (.PC(PC_t), .Addr(Addr), .Fetch(Fetch), .Load(Load), .Store(Store), .MemRegVal(regval_1_arith));
  // Probe on Addr
  // Probe on SP_1
  // Probe on R0
  // Probe on R3
  // Probe on R6
  // Probe on MemIN
  Subtractor #(.width(16)) subtractor_2 (.a(SP), .b(16'h1), .out(subtractor_2_out));  // open: bin, bout
  Adder #(.width(16)) adder_2 (.a(PC), .b(16'h1), .out(adder_2_out));  // open: cin, cout
  // Probe on R1
  // Probe on R4
  // Probe on R7
  assign bit_extender_1_out = {{16{MemIN[15]}}, MemIN};  // Bit_Extender bit_extender_1
  Multiplexer #(.width(16)) multiplexer_1 (
    .in0(subtractor_2_out), .in1(SP), .out(multiplexer_1_out), .sel(Call));  // open: en
  // Probe on multiplexer_1_out
  // Probe on R2
  // Probe on R5
  DecodeIR decodeir_1 (
    .CTRL(CTRL), .IR(IR), .Load(Load), .GetOp(GetOp), .Store(Store), .WriteReg(WriteReg),
    .JMPAddress(JMP_Address), .MemReg(MemReg), .CALL(Call), .RET(Ret));
  RamCtrl ramctrl_1 (
    .Store(Store), .Fetch(Fetch), .Exec(Exec), .Load(Load), .MemStore(ramctrl_1_memstore),
    .MemLoad(ramctrl_1_memload), .Clock(Clock));
  RAM #(.addrWidth(16), .dataWidth(32), .bus("separate")) ram_1 (
    .addr(Addr), .din(bit_extender_1_out), .data(MemOUT), .str(ramctrl_1_memstore), .clk(ramctrl_1_memstore),
    .ld(ramctrl_1_memload), .clr(ResetRAM));  // open: sel
  // Probe on StackAddr
  RAM #(.addrWidth(16), .dataWidth(16), .bus("separate")) ram_2 (
    .addr(multiplexer_1_out), .din(adder_2_out), .data(StackAddr), .str(Call), .clk(Clock), .clr(Reset));  // open: sel, ld
  // Probe on MemOUT
  Register #(.width(32), .trigger("falling")) RegIR (.D(MemOUT), .Q(IR), .clk(Fetch), .clr(Reset));  // open: en
  // Probe on MemIN
  // Probe on MemReg
  JMPCond jmpcond_1 (
    .IR(IR), .Cond(Cond), .in_2(R0), .in_3(R1), .in_4(R2), .in_5(R3), .in_6(R4), .in_7(R5), .in_8(R6),
    .in_9(R7));
  // Probe on IR
  // Probe on IR[8:6]
  // Probe on IR[11:9]
  // Probe on IR[14:12]
  // Probe on getcst_1_cst
  GetCst getcst_1 (.IR(IR), .Cst(getcst_1_cst), .Imm(getcst_1_imm));
  // Probe on GetOp
  // Probe on MemOUT
  // Probe on JMP_Address
  Registres registres_1 (
    .IN(multiplexer_2_out), .WriteReg(WriteReg), .DR(IR[8:6]), .R0(R0), .R1(R1), .R2(R2), .R3(R3), .R4(R4),
    .R5(R5), .R6(R6), .R7(R7), .Reset(Reset), .Clock(Exec), .OUT_DR(MemIN), .SR2(IR[11:9]),
    .OUT_SR2(registres_1_out_sr2), .OUT_SR1(registres_1_out_sr1), .SR1(IR[14:12]));
  // Probe on registres_1_out_sr1
  ALU alu_1 (
    .Imm(getcst_1_imm), .e2(GetOp), .Input1(registres_1_out_sr1), .Input2(registres_1_out_sr2),
    .Cst(getcst_1_cst), .Output(alu_1_output));
  Multiplexer #(.width(16)) multiplexer_2 (
    .in0(alu_1_output), .in1(MemOUT[15:0]), .out(multiplexer_2_out), .sel(Load));  // open: en
  // Probe on multiplexer_2_out
  // Probe on registres_1_out_sr2
  // Probe on R0
  // Probe on R1
  // Probe on R2
  // Probe on R3
  // Probe on R4
  // Probe on R5
  // Probe on R6
  // Probe on R7
  // Probe on alu_1_output

  // Other names for the same wires on the sheet: SPCall = Call; SPRet = Ret

  // Notes on the sheet:
  //   Reg SP
  //   RAM
endmodule

module ALU (
  input  [15:0] Input2,
  input  [15:0] Input1,
  input  [15:0] Cst,
  input  Imm,
  input  [2:0] e2,
  output [15:0] Output
);

  wire [15:0] I2, Res_ADD, Res_AND, Res_MUL, Res_OR, Res_SL, Res_SR, Res_SUB, Res_XOR;

  Adder #(.width(16)) adder_1 (.a(Input2), .b(I2), .out(Res_ADD));  // open: cin, cout
  Subtractor #(.width(16)) subtractor_1 (.a(Input2), .b(I2), .out(Res_SUB));  // open: bin, bout
  Multiplier #(.width(16)) multiplier_1 (.a(Input2), .b(I2), .out(Res_MUL));  // open: cin, cout
  Multiplexer #(.width(16)) multiplexer_1 (.in0(Input1), .in1(Cst), .out(I2), .sel(Imm));  // open: en
  // Probe on I2
  Multiplexer #(.select(3), .width(16)) multiplexer_2 (
    .in0(Res_ADD), .in1(Res_SUB), .in2(Res_AND), .in3(Res_OR), .in4(Res_XOR), .in5(Res_SL), .in6(Res_SR),
    .in7(Res_MUL), .out(Output), .sel(e2));  // open: en
  assign Res_AND = Input2 & I2;  // AND_Gate and_1, 16 bits wide
  assign Res_OR = Input2 | I2;  // OR_Gate or_1, 16 bits wide
  assign Res_XOR = Input2 ^ I2;  // XOR_Gate xor_1, 16 bits wide
  Shifter #(.width(16)) shifter_1 (.in(Input2), .\dist (I2[3:0]), .out(Res_SL));
  Shifter #(.width(16), .shift("ar")) shifter_2 (.in(Input2), .\dist (I2[3:0]), .out(Res_SR));

  // Other names for the same wires on the sheet: I1[15:0] = Input2
endmodule

module DecodeIR (
  input  [31:0] IR,
  output WriteReg,
  output [2:0] MemReg,
  output CTRL,
  output [15:0] JMPAddress,
  output Load,
  output Store,
  output CALL,
  output RET,
  output [2:0] GetOp
);

  wire and_5_out, and_6_out, JMPSimple, not_1_out, not_2_out, not_3_out, not_4_out, not_5_out, not_6_out,
       not_7_out, not_8_out, not_9_out, not_10_out, not_11_out, not_12_out, or_1_out;

  // Probe on IR[20:5]
  Multiplexer #(.width(16)) multiplexer_1 (
    .in0(IR[20:5]), .in1(IR[26:11]), .out(JMPAddress), .sel(not_1_out));  // open: en
  // Probe on IR[26:11]
  not not_1 (not_1_out, or_1_out);
  or or_1 (or_1_out, JMPSimple, CALL);
  not not_2 (not_2_out, IR[2]);
  not not_3 (not_3_out, IR[4]);
  not not_4 (not_4_out, IR[3]);
  and and_1 (JMPSimple, not_2_out, not_4_out, not_3_out);
  not not_5 (not_5_out, IR[2]);
  not not_6 (not_6_out, IR[3]);
  not not_7 (not_7_out, IR[3]);
  not not_8 (not_8_out, IR[4]);
  not not_9 (not_9_out, IR[0]);
  and and_2 (CALL, IR[2], not_7_out, IR[4], CTRL);
  and and_3 (RET, CTRL, IR[2], IR[3], not_8_out);
  not not_10 (not_10_out, IR[1]);
  not not_11 (not_11_out, IR[0]);
  and and_4 (CTRL, IR[1], IR[0]);
  and and_5 (and_5_out, not_9_out, IR[1]);
  not not_12 (not_12_out, IR[4]);
  and and_6 (and_6_out, not_10_out, not_11_out);
  and and_7 (Load, and_5_out, not_5_out, not_6_out, not_12_out);
  and and_8 (Store, and_5_out, not_5_out, not_6_out, IR[4]);
  or or_2 (WriteReg, and_6_out, Load);

  assign GetOp = {IR[2], IR[3], IR[4]};
  assign MemReg = IR[11:9];

  // Notes on the sheet:
  //   MEM : 01
  //   CALL : 101
  //   RET : 110
  //   CTRL : 11
  //   ARITHM. : 00
  //   Load : 000
  //   Store : 001
endmodule

module GetAddr (
  input  [15:0] MemRegVal,
  input  [15:0] PC,
  input  Fetch,
  input  Load,
  input  Store,
  output [15:0] Addr
);

  wire or_1_out;

  or or_1 (or_1_out, Fetch, Load, Store);
  Multiplexer #(.width(16)) multiplexer_1 (.in0(MemRegVal), .in1(PC), .out(Addr), .sel(Fetch), .en(or_1_out));

  // Notes on the sheet:
  //   Valeur contenue dans le registre d'adresse
endmodule

module GetCst (
  input  [31:0] IR,
  output [15:0] Cst,
  output Imm
);

  // Probe on Cst
  Bit_Extender #(.in_width(20)) bit_extender_1 (.in(IR[31:12]), .out(Cst));
  // Probe on {IR[12], IR[13], IR[14], IR[15], IR[16], IR[17], IR[18], IR[19], IR[20], IR[21], IR[22], IR[23], IR[24], IR[25], IR[26], IR[27]}

  assign Imm = IR[5];
endmodule

module RamCtrl (
  input  Clock,
  input  Exec,
  input  Fetch,
  input  Load,
  input  Store,
  output MemLoad,
  output MemStore
);

  wire and_1_out;

  and and_1 (and_1_out, Exec, Load);
  and and_2 (MemStore, Exec, Clock, Store);
  or or_1 (MemLoad, Fetch, and_1_out);
endmodule

module Registres (
  input  [15:0] IN,
  input  [2:0] DR,
  input  [2:0] SR1,
  input  [2:0] SR2,
  input  Clock,
  input  Reset,
  input  WriteReg,
  output [15:0] R0,
  output [15:0] OUT_DR,
  output [15:0] R1,
  output [15:0] R2,
  output [15:0] R3,
  output [15:0] OUT_SR1,
  output [15:0] R4,
  output [15:0] R5,
  output [15:0] R6,
  output [15:0] OUT_SR2,
  output [15:0] R7
);

  wire and_1_out, and_2_out, and_3_out, and_4_out, and_5_out, and_6_out, and_7_out, and_8_out, and_9_out,
       decoder_1_out0, decoder_1_out1, decoder_1_out2, decoder_1_out3, decoder_1_out4, decoder_1_out5,
       decoder_1_out6, decoder_1_out7;

  Decoder #(.select(3)) decoder_1 (
    .out0(decoder_1_out0), .out1(decoder_1_out1), .out2(decoder_1_out2), .out3(decoder_1_out3),
    .out4(decoder_1_out4), .out5(decoder_1_out5), .out6(decoder_1_out6), .out7(decoder_1_out7), .sel(DR));  // open: en
  and and_1 (and_1_out, WriteReg, Clock);
  and and_2 (and_2_out, decoder_1_out0, and_1_out);
  and and_3 (and_3_out, decoder_1_out1, and_1_out);
  and and_4 (and_4_out, decoder_1_out2, and_1_out);
  and and_5 (and_5_out, decoder_1_out3, and_1_out);
  and and_6 (and_6_out, decoder_1_out4, and_1_out);
  and and_7 (and_7_out, decoder_1_out5, and_1_out);
  and and_8 (and_8_out, decoder_1_out6, and_1_out);
  and and_9 (and_9_out, decoder_1_out7, and_1_out);
  Register #(.width(16), .trigger("falling")) u_R0 (.D(IN), .en(and_2_out), .Q(R0), .clk(Clock), .clr(Reset));
  Register #(.width(16), .trigger("falling")) u_R1 (.D(IN), .en(and_3_out), .Q(R1), .clk(Clock), .clr(Reset));
  Register #(.width(16), .trigger("falling")) u_R2 (.D(IN), .en(and_4_out), .Q(R2), .clk(Clock), .clr(Reset));
  Register #(.width(16), .trigger("falling")) u_R3 (.D(IN), .en(and_5_out), .Q(R3), .clk(Clock), .clr(Reset));
  Register #(.width(16), .trigger("falling")) u_R4 (.D(IN), .en(and_6_out), .Q(R4), .clk(Clock), .clr(Reset));
  Register #(.width(16), .trigger("falling")) u_R5 (.D(IN), .en(and_7_out), .Q(R5), .clk(Clock), .clr(Reset));
  Register #(.width(16), .trigger("falling")) u_R6 (.D(IN), .en(and_8_out), .Q(R6), .clk(Clock), .clr(Reset));
  Register #(.width(16), .trigger("falling")) u_R7 (.D(IN), .en(and_9_out), .Q(R7), .clk(Clock), .clr(Reset));
  Multiplexer #(.select(3), .width(16)) multiplexer_1 (
    .in0(R0), .in1(R1), .in2(R2), .in3(R3), .in4(R4), .in5(R5), .in6(R7), .in7(R7), .out(OUT_DR), .sel(DR));  // open: en
  Multiplexer #(.select(3), .width(16)) multiplexer_2 (
    .in0(R0), .in1(R1), .in2(R2), .in3(R3), .in4(R4), .in5(R5), .in6(R7), .in7(R7), .out(OUT_SR1), .sel(SR1));  // open: en
  Multiplexer #(.select(3), .width(16)) multiplexer_3 (
    .in0(R0), .in1(R1), .in2(R2), .in3(R3), .in4(R4), .in5(R5), .in6(R7), .in7(R7), .out(OUT_SR2), .sel(SR2));  // open: en

  // Other names for the same wires on the sheet: Write = WriteReg
endmodule

module RegPC (
  input  [15:0] JMP_Address,
  input  Cond,
  input  CTRL,
  input  [15:0] RET_Address,
  input  Call,
  input  RET,
  input  Clock,
  input  Reset,
  output [15:0] PC
);

  wire and_1_out, and_2_out, or_1_out;
  wire [15:0] multiplexer_1_out, PC_1, PC_q;

  and and_1 (and_1_out, Cond, CTRL);
  or or_1 (or_1_out, and_1_out, and_2_out);
  and and_2 (and_2_out, CTRL, Call);
  Multiplexer #(.width(16)) multiplexer_1 (
    .in0(PC_1), .in1(JMP_Address), .out(multiplexer_1_out), .sel(or_1_out));  // open: en
  // Probe on multiplexer_1_out
  Register #(.width(16), .trigger("falling")) u_PC (
    .D(multiplexer_1_out), .Q(PC_q), .clk(Clock), .clr(Reset));  // open: en
  Adder #(.width(16)) adder_1 (.a(16'h1), .b(PC_q), .out(PC_1), .cin(1'b0));  // open: cout
  Multiplexer #(.width(16)) multiplexer_2 (.in0(PC_q), .in1(RET_Address), .out(PC), .sel(RET));  // open: en
endmodule

module Seq (
  input  ClockOrig,
  input  reset,
  output Fetch,
  output Exec,
  output Clock
);

  Register #(.width(1), .trigger("falling")) register_1 (
    .D(Fetch), .Q(Exec), .clk(ClockOrig), .clr(reset));  // open: en
  not not_1 (Fetch, Exec);
  buf buffer_1 (Clock, ClockOrig);
endmodule

module RegVal (
  input  [15:0] R0,
  input  [15:0] R1,
  input  [15:0] R2,
  input  [15:0] R3,
  input  [15:0] R4,
  input  [15:0] R5,
  input  [2:0] Reg,
  input  [15:0] R6,
  input  [15:0] R7,
  output [15:0] Arith
);

  Multiplexer #(.select(3), .width(16)) multiplexer_1 (
    .in0(R0), .in1(R1), .in2(R2), .in3(R3), .in4(R4), .in5(R5), .in6(R6), .in7(R7), .out(Arith), .sel(Reg));  // open: en
endmodule

module JMPCond (
  input  [31:0] IR,
  input  [15:0] in_2,
  input  [15:0] in_3,
  input  [15:0] in_4,
  input  [15:0] in_5,
  input  [15:0] in_6,
  input  [15:0] in_7,
  input  [15:0] in_8,
  input  [15:0] in_9,
  output Cond
);

  wire and_1_out, JEQU, JINF, JNEQ, JSUP, multiplexer_1_out;
  wire [15:0] Reg1, Reg2;

  // Probe on IR[7:5]
  // Probe on IR[10:8]
  RegVal regval_1 (
    .R0(in_2), .R1(in_3), .R2(in_4), .R3(in_5), .R4(in_6), .R5(in_7), .Reg(IR[7:5]), .R6(in_8), .R7(in_9),
    .Arith(Reg1));
  RegVal regval_2 (
    .R0(in_2), .R1(in_3), .R2(in_4), .R3(in_5), .R4(in_6), .R5(in_7), .Reg(IR[10:8]), .R6(in_8), .R7(in_9),
    .Arith(Reg2));
  Comparator #(.width(16)) comparator_1 (.a(Reg1), .b(Reg2), .gt(JSUP), .eq(JEQU), .lt(JINF));
  not not_1 (JNEQ, JEQU);
  and and_1 (and_1_out, IR[0], IR[1]);
  and and_2 (Cond, and_1_out, multiplexer_1_out);
  Multiplexer #(.select(3)) multiplexer_1 (
    .in0(1'b1), .in1(JEQU), .in2(JSUP), .in3(JNEQ), .in4(JINF), .in5(1'b1), .in6(1'b1), .in7(1'b0),
    .out(multiplexer_1_out), .sel({IR[2], IR[3], IR[4]}));  // open: en
  // Probe on {IR[2], IR[3], IR[4]}

  // Other names for the same wires on the sheet: RCond1[2:0] = IR[7:5]; RCond2[2:0] = IR[10:8]; R0[15:0] = in_2;
  //   R1[15:0] = in_3; R2[15:0] = in_4; R3[15:0] = in_5; R4[15:0] = in_6; R5[15:0] = in_7; R6[15:0] = in_8;
  //   R7[15:0] = in_9

  // Notes on the sheet:
  //   Verif si operation de controle
  //   JMP (tjs actif)
  //   (rien)
endmodule

module Pile (
  input  [15:0] PC,
  input  Clock,
  input  Reset,
  input  Call,
  input  Ret,
  output [15:0] StackAddr
);

  wire or_1_out;
  wire [15:0] adder_1_out, adder_2_out, SP, SP_1, subtractor_1_out;

  Adder #(.width(16)) adder_1 (.a(SP), .b(16'h1), .out(adder_1_out));  // open: cin, cout
  Subtractor #(.width(16)) subtractor_1 (.a(SP), .b(16'h1), .out(subtractor_1_out));  // open: bin, bout
  Register #(.width(16)) register_1 (.D(SP_1), .en(or_1_out), .Q(SP), .clk(Clock), .clr(Reset));
  or or_1 (or_1_out, Call, Ret);
  assign SP_1 = Call ? adder_1_out : 16'bz;  // Controlled_Buffer controlled_buffer_1
  // Probe on SP_1
  assign SP_1 = Ret ? subtractor_1_out : 16'bz;  // Controlled_Buffer controlled_buffer_2
  Adder #(.width(16)) adder_2 (.a(PC), .b(16'h1), .out(adder_2_out));  // open: cin, cout
  RAM #(.addrWidth(16), .dataWidth(16), .bus("separate")) ram_1 (
    .addr(SP), .din(adder_2_out), .data(StackAddr), .str(Call), .clk(Clock), .ld(Ret), .clr(Reset));  // open: sel

  // Notes on the sheet:
  //   Reg SP
endmodule
